// Logisim project umips.circ as structural Verilog: 6 circuits, main circuit main
module main (
);

  wire add_sub, Addi, AInv, alu_1_compare, and_1_p1, and_1_p2, and_2_out, and_3_out, and_4_out, and_6_p2,
       and_nor, BInv, bp_n, bx_z, Clock, Dis_enable, div_mul, halt, j, jal, jr, Li, lw_sw, MemtoReg,
       not_1_p1, not_3_p2, not_4_p2, not_5_out, not_7_out, or_1_out, or_2_out, or_3_out, or_4_out,
       R_ISplitter_r_i, sllv_slrv, SubOpI, WriteEn;
  wire [1:0] ALUOp, pcselect, priority_encoder_2_out;
  wire [2:0] i_instruction_splitter_1_opcode, i_instruction_splitter_1_rs, multiplexer_3_out,
       multiplexer_4_out, r_instruction_splitter_1_opcode, r_instruction_splitter_1_rs,
       r_instruction_splitter_1_rt;
  wire [7:0] Immediate, multiplexer_1_out, PC, register_1_q;
  wire [14:0] demultiplexer_1_out0, demultiplexer_1_out1, R_ISplitter_instruction15;
  wire [15:0] alu_2_result, and_7_out, and_8_out, bit_extender_1_out, bit_extender_2_out, bit_extender_3_out,
       Display_Controller_q, divider_1_out, divider_1_rem, mul_div_hi, mul_div_lo, multiplexer_2_out,
       multiplexer_5_out, multiplexer_6_out, multiplexer_10_out, multiplexer_11_out, multiplier_1_cout,
       multiplier_1_out, Put, ram_1_data, rom_1_data, rt, shift_result, shifter_1_out, shifter_2_out;

  Multiplexer #(.select(2), .width(8), .disabled(0)) multiplexer_1 (
    .in0(PC), .in1(Immediate), .in2(Put[7:0]), .in3(Immediate), .out(multiplexer_1_out), .sel(pcselect));  // open: en
  LED led_1 (.in(halt));
  Clock clock_1 (.out(Clock));
  Register #(.width(16)) Display_Controller (
    .D(Put), .en(Dis_enable), .Q(Display_Controller_q), .clk(not_1_p1));  // open: clr
  // NOT_Gate not_1: pin names not known; wires that end beside it: not_1_p1, Clock
  Adder adder_1 (.a(register_1_q), .b(8'h1), .out(PC));  // open: cin, cout
  // AND_Gate and_1: pin names not known; wires that end beside it: and_1_p1, and_1_p2, 1'b1
  not not_2 (and_1_p1, halt);
  Hex_Digit_Display hex_digit_display_1 (.value(Display_Controller_q[15:12]));  // open: dp
  Register register_1 (.D(multiplexer_1_out), .en(and_1_p2), .Q(register_1_q), .clk(Clock));  // open: clr
  Hex_Digit_Display hex_digit_display_2 (.value(Display_Controller_q[7:4]));  // open: dp
  Hex_Digit_Display hex_digit_display_3 (.value(Display_Controller_q[11:8]));  // open: dp
  // Probe on Put
  Hex_Digit_Display hex_digit_display_4 (.value(Display_Controller_q[3:0]));  // open: dp
  ALU alu_1 (
    .A(Put), .B({16{1'b0}}), .Compare(alu_1_compare), .ALUComp(bx_z), .Op(SubOpI));  // open: Result, B_Invert, A_Invert, ALUop
  and and_2 (and_2_out, bp_n, alu_1_compare);
  // NOT_Gate not_3: pin names not known; wires that end beside it: alu_1_compare, not_3_p2
  RISplitter R_ISplitter (.Instruction(rom_1_data), .R_I(R_ISplitter_r_i), .Instruction15(R_ISplitter_instruction15));
  ROM #(.dataWidth(16)) rom_1 (.addr(register_1_q), .data(rom_1_data), .sel(1'b1));
  Demultiplexer #(.width(15)) demultiplexer_1 (
    .out0(demultiplexer_1_out0), .out1(demultiplexer_1_out1), .in(R_ISplitter_instruction15),
    .sel(R_ISplitter_r_i));  // open: en
  // NOT_Gate not_4: pin names not known; wires that end beside it: SubOpI, not_4_p2
  Demultiplexer #(.select(3), .disabled(0), .enable("true")) demultiplexer_2 (
    .out0(Addi), .out1(Li), .out2(bp_n), .out3(bx_z), .out4(jal), .out5(j), .in(1'b1),
    .sel(i_instruction_splitter_1_opcode), .en(R_ISplitter_r_i));  // open: out6, out7
  Demultiplexer #(.select(3), .disabled(0), .enable("true")) demultiplexer_3 (
    .out0(and_nor), .out1(add_sub), .out2(sllv_slrv), .out3(div_mul), .out4(lw_sw), .out5(jr), .out6(halt),
    .out7(Dis_enable), .in(1'b1), .sel(r_instruction_splitter_1_opcode), .en(not_5_out));
  and and_3 (and_3_out, alu_1_compare, bx_z, SubOpI);
  and and_4 (and_4_out, not_4_p2, bx_z, not_3_p2);
  I_Instruction_Splitter i_instruction_splitter_1 (
    .Instruction(demultiplexer_1_out1), .Rs(i_instruction_splitter_1_rs), .Imm(Immediate), .Subop(SubOpI),
    .Opcode(i_instruction_splitter_1_opcode));
  R_Instruction_Splitter r_instruction_splitter_1 (
    .Instruction(demultiplexer_1_out0), .Rs(r_instruction_splitter_1_rs), .Rt(r_instruction_splitter_1_rt),
    .Subop(BInv), .Opcode(r_instruction_splitter_1_opcode));
  not not_5 (not_5_out, R_ISplitter_r_i);
  and and_5 (AInv, and_nor, BInv);
  or or_1 (or_1_out, and_2_out, and_3_out, and_4_out);
  assign bit_extender_1_out = {{8{1'b0}}, Immediate};  // Bit_Extender bit_extender_1
  assign bit_extender_2_out = {{8{Immediate[7]}}, Immediate};  // Bit_Extender bit_extender_2
  Priority_Encoder #(.select(2)) priority_encoder_1 (
    .in0(1'b1), .in1(or_1_out), .in2(jr), .in3(or_2_out), .out(pcselect));  // open: gs, en_out, en_in
  or or_2 (or_2_out, jal, j);
  Multiplexer #(.width(16), .disabled(0)) multiplexer_2 (
    .in0(bit_extender_1_out), .in1(bit_extender_2_out), .out(multiplexer_2_out), .sel(SubOpI));  // open: en
  or or_3 (or_3_out, add_sub, Addi);
  // Probe on i_instruction_splitter_1_rs
  Multiplexer #(.width(3), .disabled(0)) multiplexer_3 (
    .in0(r_instruction_splitter_1_rs), .in1(i_instruction_splitter_1_rs), .out(multiplexer_3_out),
    .sel(R_ISplitter_r_i));  // open: en
  // AND_Gate and_6: pin names not known; wires that end beside it: lw_sw, and_6_p2, MemtoReg
  not not_6 (and_6_p2, BInv);
  // Probe on multiplexer_4_out
  Multiplexer #(.width(3), .disabled(0)) multiplexer_4 (
    .in0(r_instruction_splitter_1_rs), .in1(i_instruction_splitter_1_rs), .out(multiplexer_4_out),
    .sel(R_ISplitter_r_i));  // open: en
  // Probe on priority_encoder_2_out
  Priority_Encoder #(.select(2)) priority_encoder_2 (
    .in0(1'b1), .in1(Li), .in2(div_mul), .in3(sllv_slrv), .out(priority_encoder_2_out));  // open: gs, en_out, en_in
  // Probe on ALUOp
  Priority_Encoder #(.select(2)) priority_encoder_3 (
    .in0(1'b1), .in1(or_3_out), .out(ALUOp));  // open: in2, in3, gs, en_out, en_in
  // Probe on multiplexer_2_out
  // Probe on r_instruction_splitter_1_rt
  Multiplexer #(.select(2), .width(16), .disabled(0)) multiplexer_5 (
    .in0(multiplexer_11_out), .in1(multiplexer_2_out), .in2(mul_div_lo), .in3(shift_result),
    .out(multiplexer_5_out), .sel(priority_encoder_2_out));  // open: en
  or or_4 (or_4_out, sllv_slrv, sllv_slrv, jal);
  or or_5 (WriteEn, MemtoReg, Li, add_sub, div_mul, Addi, and_nor, or_4_out);
  // Probe on multiplexer_5_out
  // Probe on and_7_out
  assign and_7_out = rt & 16'hf;  // AND_Gate and_7, 16 bits wide
  Register_File register_file_1 (
    .ReadRegister1(multiplexer_3_out), .ReadRegister2(r_instruction_splitter_1_rt),
    .WriteRegister(multiplexer_4_out), .WriteData(multiplexer_5_out), .ReadData1(Put), .ReadData2(rt),
    .WriteEnable(WriteEn), .Clock(Clock), .WriteEnable2(div_mul), .WriteData2(mul_div_hi));
  Multiplexer #(.width(16), .disabled(0)) multiplexer_6 (
    .in0(rt), .in1(multiplexer_2_out), .out(multiplexer_6_out), .sel(Addi));  // open: en
  Shifter #(.width(16)) shifter_1 (.in(Put), .\dist (and_7_out[3:0]), .out(shifter_1_out));
  Shifter #(.width(16), .shift("lr")) shifter_2 (.in(Put), .\dist (and_7_out[3:0]), .out(shifter_2_out));
  // Probe on Put
  Divider #(.width(16)) divider_1 (.a(Put), .b(rt), .out(divider_1_out), .rem(divider_1_rem));  // open: upper
  Multiplexer #(.width(16), .disabled(0)) multiplexer_7 (
    .in0(shifter_1_out), .in1(shifter_2_out), .out(shift_result), .sel(BInv));  // open: en
  ALU alu_2 (
    .A(Put), .B(multiplexer_6_out), .Result(alu_2_result), .B_Invert(BInv), .A_Invert(AInv), .ALUop(ALUOp));  // open: Compare, ALUComp, Op
  Multiplier #(.width(16)) multiplier_1 (
    .a(Put), .b(rt), .out(multiplier_1_out), .cout(multiplier_1_cout));  // open: cin
  Multiplexer #(.width(16), .disabled(0)) multiplexer_8 (
    .in0(divider_1_rem), .in1(multiplier_1_cout), .out(mul_div_hi), .sel(BInv));  // open: en
  // Probe on and_8_out
  assign and_8_out = rt & 16'hff;  // AND_Gate and_8, 16 bits wide
  // Multiplexer #(.width(16), .disabled(0)) multiplexer_9: pin names not known; wires that end beside it: divider_1_out, multiplier_1_out, BInv, mul_div_lo
  not not_7 (not_7_out, Clock);
  // Probe on ram_1_data
  RAM #(.addrWidth(16), .dataWidth(16), .bus("separate")) ram_1 (
    .addr(and_8_out), .din(Put), .data(ram_1_data), .str(BInv), .sel(lw_sw), .clk(Clock), .ld(not_7_out));  // open: clr
  // Probe on multiplexer_11_out
  Multiplexer #(.width(16), .disabled(0)) multiplexer_10 (
    .in0(alu_2_result), .in1(ram_1_data), .out(multiplexer_10_out), .sel(MemtoReg));  // open: en
  Multiplexer #(.width(16), .disabled(0)) multiplexer_11 (
    .in0(multiplexer_10_out), .in1(bit_extender_3_out), .out(multiplexer_11_out), .sel(jal));  // open: en
  assign bit_extender_3_out = {{8{1'b0}}, PC};  // Bit_Extender bit_extender_3

  // Other names for the same wires on the sheet: rs[15:0] = Put; SubOpR = BInv

  // Notes on the sheet:
  //   Matthew Sivaprakasam
  //   mjs299@pitt.edu
  //   contents of rom_1 (hex, n*v repeats v):
  //   9c00 920a ce0a 7200 6000 9404 1441 a415 9202 d03c 4381 8c03 4f81 8c03 83ff 7200 ce0a 4381 8c03 8dfb
  //   4380 8c07 83fd ce0a 8dff 4580 1280 8dff 4f80 8dff 5e00
endmodule

module R_Instruction_Splitter (
  input  [14:0] Instruction,
  output [2:0] Rs,
  output [2:0] Rt,
  output Subop,
  output [2:0] Opcode
);


  assign Opcode = Instruction[14:12];
  assign Rs = Instruction[11:9];
  assign Rt = Instruction[8:6];
  assign Subop = Instruction[0];
endmodule

module RISplitter (
  input  [15:0] Instruction,
  output R_I,
  output [14:0] Instruction15
);


  assign Instruction15 = Instruction[14:0];
  assign R_I = Instruction[15];
endmodule

module I_Instruction_Splitter (
  input  [14:0] Instruction,
  output [2:0] Rs,
  output [7:0] Imm,
  output Subop,
  output [2:0] Opcode
);


  assign Imm = Instruction[8:1];
  assign Opcode = Instruction[14:12];
  assign Rs = Instruction[11:9];
  assign Subop = Instruction[0];
endmodule

module Register_File (
  input  [15:0] WriteData2,
  input  WriteEnable,
  input  [2:0] ReadRegister1,
  input  [2:0] ReadRegister2,
  input  [2:0] WriteRegister,
  input  [15:0] WriteData,
  input  Clock,
  input  WriteEnable2,
  output [15:0] ReadData1,
  output [15:0] ReadData2
);

  wire demultiplexer_1_out0, demultiplexer_1_out1, demultiplexer_1_out2, demultiplexer_1_out3,
       demultiplexer_1_out4, demultiplexer_1_out5, demultiplexer_1_out6, demultiplexer_1_out7,
       demultiplexer_3_out0, demultiplexer_3_out1, demultiplexer_3_out2, demultiplexer_3_out3,
       demultiplexer_3_out4, demultiplexer_3_out5, demultiplexer_3_out6, demultiplexer_3_out7, or_1_out,
       or_2_p4, or_3_p5, or_4_p4, or_5_out, or_6_p3, or_7_p3, or_8_out;
  wire [2:0] W2Sel;
  wire [15:0] demultiplexer_2_out0, demultiplexer_2_out1, demultiplexer_2_out2, demultiplexer_2_out3,
       demultiplexer_2_out4, demultiplexer_2_out5, demultiplexer_2_out6, demultiplexer_2_out7,
       demultiplexer_4_out0, demultiplexer_4_out1, demultiplexer_4_out2, demultiplexer_4_out3,
       demultiplexer_4_out4, demultiplexer_4_out5, demultiplexer_4_out6, demultiplexer_4_out7,
       multiplexer_1_out, multiplexer_2_out, multiplexer_3_out, multiplexer_4_out, multiplexer_5_out,
       multiplexer_6_out, multiplexer_7_out, multiplexer_8_out, Register0_q, Register1_q, Register2_q,
       Register3_q, Register4_q, Register5_q, Register6_q, Register7_q;

  Demultiplexer #(.select(3)) demultiplexer_1 (
    .out0(demultiplexer_1_out0), .out1(demultiplexer_1_out1), .out2(demultiplexer_1_out2),
    .out3(demultiplexer_1_out3), .out4(demultiplexer_1_out4), .out5(demultiplexer_1_out5),
    .out6(demultiplexer_1_out6), .out7(demultiplexer_1_out7), .in(WriteEnable), .sel(WriteRegister));  // open: en
  Demultiplexer #(.select(3), .width(16)) demultiplexer_2 (
    .out0(demultiplexer_2_out0), .out1(demultiplexer_2_out1), .out2(demultiplexer_2_out2),
    .out3(demultiplexer_2_out3), .out4(demultiplexer_2_out4), .out5(demultiplexer_2_out5),
    .out6(demultiplexer_2_out6), .out7(demultiplexer_2_out7), .in(WriteData), .sel(WriteRegister));  // open: en
  Adder #(.width(3)) adder_1 (.a(WriteRegister), .b(3'b001), .out(W2Sel));  // open: cin, cout
  // Probe on W2Sel
  Demultiplexer #(.select(3)) demultiplexer_3 (
    .out0(demultiplexer_3_out0), .out1(demultiplexer_3_out1), .out2(demultiplexer_3_out2),
    .out3(demultiplexer_3_out3), .out4(demultiplexer_3_out4), .out5(demultiplexer_3_out5),
    .out6(demultiplexer_3_out6), .out7(demultiplexer_3_out7), .in(WriteEnable2), .sel(W2Sel));  // open: en
  Demultiplexer #(.select(3), .width(16)) demultiplexer_4 (
    .out0(demultiplexer_4_out0), .out1(demultiplexer_4_out1), .out2(demultiplexer_4_out2),
    .out3(demultiplexer_4_out3), .out4(demultiplexer_4_out4), .out5(demultiplexer_4_out5),
    .out6(demultiplexer_4_out6), .out7(demultiplexer_4_out7), .in(WriteData2), .sel(W2Sel));  // open: en
  or or_1 (or_1_out, demultiplexer_1_out0, demultiplexer_3_out0);
  // OR_Gate or_2: pin names not known; wires that end beside it: demultiplexer_1_out1, demultiplexer_1_out1, demultiplexer_3_out1, or_2_p4
  // OR_Gate or_3: pin names not known; wires that end beside it: demultiplexer_3_out1, demultiplexer_1_out2, demultiplexer_1_out2, demultiplexer_3_out2, or_3_p5
  // OR_Gate or_4: pin names not known; wires that end beside it: demultiplexer_1_out3, demultiplexer_3_out4, demultiplexer_3_out3, or_4_p4
  or or_5 (or_5_out, demultiplexer_1_out4, demultiplexer_3_out4);
  // OR_Gate or_6: pin names not known; wires that end beside it: demultiplexer_1_out5, demultiplexer_3_out5, or_6_p3
  // OR_Gate or_7: pin names not known; wires that end beside it: demultiplexer_1_out6, demultiplexer_3_out6, or_7_p3
  or or_8 (or_8_out, demultiplexer_1_out7, demultiplexer_3_out7);
  Multiplexer #(.width(16), .disabled(0)) multiplexer_1 (
    .in0(demultiplexer_2_out1), .in1(demultiplexer_4_out1), .out(multiplexer_1_out),
    .sel(demultiplexer_3_out1));  // open: en
  Multiplexer #(.width(16), .disabled(0)) multiplexer_2 (
    .in0(demultiplexer_2_out2), .in1(demultiplexer_4_out2), .out(multiplexer_2_out),
    .sel(demultiplexer_3_out2));  // open: en
  Multiplexer #(.width(16), .disabled(0)) multiplexer_3 (
    .in0(demultiplexer_2_out5), .in1(demultiplexer_4_out5), .out(multiplexer_3_out),
    .sel(demultiplexer_3_out5));  // open: en
  Multiplexer #(.width(16), .disabled(0)) multiplexer_4 (
    .in0(demultiplexer_2_out0), .in1(demultiplexer_4_out0), .out(multiplexer_4_out),
    .sel(demultiplexer_3_out0));  // open: en
  Register #(.width(16)) Register0 (.D(multiplexer_4_out), .en(or_1_out), .Q(Register0_q), .clk(Clock));  // open: clr
  Register #(.width(16)) Register1 (.D(multiplexer_1_out), .en(or_2_p4), .Q(Register1_q), .clk(Clock));  // open: clr
  Register #(.width(16)) Register5 (.D(multiplexer_3_out), .en(or_6_p3), .Q(Register5_q), .clk(Clock));  // open: clr
  Register #(.width(16)) Register2 (.D(multiplexer_2_out), .en(or_3_p5), .Q(Register2_q), .clk(Clock));  // open: clr
  Multiplexer #(.width(16), .disabled(0)) multiplexer_5 (
    .in0(demultiplexer_2_out6), .in1(demultiplexer_4_out6), .out(multiplexer_5_out),
    .sel(demultiplexer_3_out6));  // open: en
  Multiplexer #(.width(16), .disabled(0)) multiplexer_6 (
    .in0(demultiplexer_2_out3), .in1(demultiplexer_4_out3), .out(multiplexer_6_out),
    .sel(demultiplexer_3_out3));  // open: en
  Register #(.width(16)) Register6 (.D(multiplexer_5_out), .en(or_7_p3), .Q(Register6_q), .clk(Clock));  // open: clr
  Multiplexer #(.width(16), .disabled(0)) multiplexer_7 (
    .in0(demultiplexer_2_out7), .in1(demultiplexer_4_out7), .out(multiplexer_7_out),
    .sel(demultiplexer_3_out7));  // open: en
  Register #(.width(16)) Register3 (.D(multiplexer_6_out), .en(or_4_p4), .Q(Register3_q), .clk(Clock));  // open: clr
  Multiplexer #(.width(16), .disabled(0)) multiplexer_8 (
    .in0(demultiplexer_2_out4), .in1(demultiplexer_4_out4), .out(multiplexer_8_out),
    .sel(demultiplexer_3_out4));  // open: en
  Register #(.width(16)) Register4 (.D(multiplexer_8_out), .en(or_5_out), .Q(Register4_q), .clk(Clock));  // open: clr
  Register #(.width(16)) Register7 (.D(multiplexer_7_out), .en(or_8_out), .Q(Register7_q), .clk(Clock));  // open: clr
  Multiplexer #(.select(3), .width(16)) multiplexer_9 (
    .in0(Register0_q), .in1(Register1_q), .in2(Register2_q), .in3(Register3_q), .in4(Register4_q),
    .in5(Register5_q), .in6(Register6_q), .in7(Register7_q), .out(ReadData1), .sel(ReadRegister1));  // open: en
  Multiplexer #(.select(3), .width(16)) multiplexer_10 (
    .in0(Register0_q), .in1(Register1_q), .in2(Register2_q), .in3(Register3_q), .in4(Register4_q),
    .in5(Register5_q), .in6(Register6_q), .in7(Register7_q), .out(ReadData2), .sel(ReadRegister2));  // open: en

  // Other names for the same wires on the sheet: Read1[2:0] = ReadRegister1; Read2[2:0] = ReadRegister2
endmodule

module ALU (
  input  A_Invert,
  input  [1:0] ALUop,
  input  ALUComp,
  input  Op,
  input  [15:0] A,
  input  B_Invert,
  input  [15:0] B,
  output [15:0] Result,
  output Compare
);

  wire adder_1_cout, comparator_1_eq, comparator_1_gt, comparator_1_lt, multiplexer_3_out;
  wire [15:0] adder_1_out, and_1_out, bit_extender_1_out, bit_extender_2_out, multiplexer_1_out,
       multiplexer_2_out, not_1_p2, not_2_p2;

  // NOT_Gate #(.width(16)) not_1: pin names not known; wires that end beside it: A, not_1_p2
  // NOT_Gate #(.width(16)) not_2: pin names not known; wires that end beside it: B, not_2_p2
  Multiplexer #(.width(16)) multiplexer_1 (
    .in0(A), .in1(not_1_p2), .out(multiplexer_1_out), .sel(A_Invert));  // open: en
  Multiplexer #(.width(16)) multiplexer_2 (
    .in0(B), .in1(not_2_p2), .out(multiplexer_2_out), .sel(B_Invert));  // open: en
  assign and_1_out = multiplexer_1_out & multiplexer_2_out;  // AND_Gate and_1, 16 bits wide
  Adder #(.width(16)) adder_1 (
    .a(multiplexer_1_out), .b(multiplexer_2_out), .out(adder_1_out), .cin(B_Invert), .cout(adder_1_cout));
  Comparator #(.width(16)) comparator_1 (
    .a(multiplexer_1_out), .b(multiplexer_2_out), .gt(comparator_1_gt), .eq(comparator_1_eq),
    .lt(comparator_1_lt));
  Multiplexer #(.disabled(0)) multiplexer_3 (
    .in0(comparator_1_gt), .in1(comparator_1_lt), .out(multiplexer_3_out), .sel(Op));  // open: en
  assign bit_extender_1_out = {{15{1'b0}}, comparator_1_gt};  // Bit_Extender bit_extender_1
  assign bit_extender_2_out = {{15{1'b0}}, comparator_1_eq};  // Bit_Extender bit_extender_2
  Multiplexer #(.disabled(0)) multiplexer_4 (
    .in0(multiplexer_3_out), .in1(comparator_1_eq), .out(Compare), .sel(ALUComp));  // open: en
  Multiplexer #(.select(2), .width(16), .disabled(0)) multiplexer_5 (
    .in0(and_1_out), .in1(adder_1_out), .in2(bit_extender_1_out), .in3(bit_extender_2_out), .out(Result),
    .sel(ALUop));  // open: en
  // Probe on Result
endmodule
